# Fritzing sketch PhotoDiodeAmp_BPW21R_TwoChannel (saved by Fritzing 0.9.3b)
breadboards: 1

parts:
  IC1 = IC, DIP package, 14 pins [chip_label=GL324]
  BATT1 = 3xAAA Switchable Battery Pack w/Bare Wire
  S1 = SPST Switch [package=switch-spdt_lock.007s]
  R1 = Resistor [tolerance=±5% resistance=100k package=THT]
  R2 = Resistor [tolerance=±5% resistance=33k package=THT]
  R3 = Resistor [tolerance=±5% resistance=68k package=THT]
  R4 = Resistor [tolerance=±5% resistance=100k package=THT]
  R5 = Resistor [tolerance=±5% resistance=1M package=THT]
  R6 = Resistor [tolerance=±5% resistance=1M package=THT]
  R7 = Resistor [tolerance=±5% resistance=1M package=THT]
  R8 = Resistor [tolerance=±5% resistance=100k package=THT]
  R9 = Rotary Potentiometer (Small) [maximum_resistance=100kΩ package=THT]
  R10 = Rotary Potentiometer (Small) [maximum_resistance=100kΩ package=THT]
  R11 = Rotary Potentiometer (Small) [maximum_resistance=100kΩ package=THT]
  R12 = Rotary Potentiometer (Small) [maximum_resistance=100kΩ package=THT]
  J1 = Screw terminal - 2 pins [package=THT]
  J2 = Screw terminal - 2 pins [package=THT]
  J3 = Screw terminal - 2 pins [package=THT]
  J4 = Screw terminal - 2 pins [package=THT]
  R13 = Resistor [tolerance=±5% resistance=1M package=THT]

nets:
  N1: IC1.pin1, R6.Pin_0, R11.leg2
  N2: IC1.pin2, R6.Pin_1, J1.pin2
  GND: IC1.pin3, IC1.pin11, IC1.pin12, BATT1.NEG, R9.leg1, R10.leg1, R11.leg1, R12.leg1, J1.pin1, J2.pin1, J3.pin1, J4.pin1
  4.5V: IC1.pin4, S1.P, R1.Pin_1, R3.Pin_1
  N3: IC1.pin5, R11.wiper
  N4: IC1.pin6, R4.Pin_0, R13.Pin_1
  N5: IC1.pin7, J2.pin2, R13.Pin_0
  N6: IC1.pin8, R7.Pin_0, J3.pin2
  N7: IC1.pin9, R7.Pin_1, R8.Pin_0
  N8: IC1.pin10, R10.wiper
  N9: IC1.pin13, R5.Pin_0, J4.pin2
  N10: IC1.pin14, R5.Pin_1, R10.leg2
  N11: BATT1.POS, S1.O
  N12: R1.Pin_0, R12.leg2
  N13: R2.Pin_0, R9.leg2
  N14: R2.Pin_1, R3.Pin_0
  N15: R4.Pin_1, R12.wiper
  N16: R8.Pin_1, R9.wiper

notes:
  In
  Out
  Out 1
  In 1
  Out 2
  In 2

custom parts:
  3xAAA Switchable Battery Pack w/Bare Wire: 3xAAA Switchable Battery Pack w/Bare Wire Connectors
