# Fritzing sketch Unified (saved by Fritzing 0.9.3b)
breadboards: 3

parts:
  MCU = Teensy 3.6 (Basic)
  U4 = LM124-324 Quad Opamp [package="DIP (Dual Inline)"]
  U6 = POT [package=pot_alpha_rv16af-20]
  U8 = POT [package=pot_alpha_rv16af-20]
  U9 = POT [package=pot_alpha_rv16af-20]
  U1 = OPA548 [package="TO220 7-Lead [THT]"]
  U10 = LM 358 Dual Op-Amp [package="DIP8 [THT]"]
  R1 = Resistor [tolerance=±5% resistance=68k package=THT]
  C2 = Electrolytic Capacitor [capacitance=1µF package="100 mil [THT, electrolytic]"]
  C3 = Electrolytic Capacitor [capacitance=1µF package="100 mil [THT, electrolytic]"]
  U11 = OPA548 [package="TO220 7-Lead [THT]"]
  R2 = Resistor [tolerance=±5% resistance=68k package=THT]
  C4 = Electrolytic Capacitor [capacitance=1µF package="100 mil [THT, electrolytic]"]
  C5 = Electrolytic Capacitor [capacitance=1µF package="100 mil [THT, electrolytic]"]
  J1 = Screw terminal - 2 pins [package=THT]
  J2 = Screw terminal - 2 pins [package=THT]
  C8 = Ceramic Capacitor [capacitance=100nF package="100 mil [THT, multilayer]"]
  C9 = Ceramic Capacitor [capacitance=100nF package="100 mil [THT, multilayer]"]
  C10 = Electrolytic Capacitor [capacitance=1µF package="100 mil [THT, electrolytic]"]
  C11 = Electrolytic Capacitor [capacitance=1µF package="100 mil [THT, electrolytic]"]
  R3 = Resistor [tolerance=±5% resistance=220k package=THT]
  R4 = Resistor [tolerance=±5% resistance=220k package=THT]
  R5 = Resistor [tolerance=±5% resistance=220k package=THT]
  R6 = Resistor [tolerance=±5% resistance=220k package=THT]
  J3 = Screw terminal - 2 pins [package=THT]
  J4 = Screw terminal - 2 pins [package=THT]
  J5 = Screw terminal - 2 pins [package=THT]
  J6 = Screw terminal - 2 pins [package=THT]
  R7 = Resistor [tolerance=±5% resistance=10k package=THT]
  R8 = Resistor [tolerance=±5% resistance=560 package=THT]
  R9 = Resistor [tolerance=±5% resistance=1M package=THT]
  C12 = Electrolytic Capacitor [capacitance=1µF package="100 mil [THT, electrolytic]"]
  R10 = Resistor [tolerance=±5% resistance=1M package=THT]
  R11 = Resistor [tolerance=±5% resistance=100k package=THT]
  R12 = Resistor [tolerance=±5% resistance=100k package=THT]
  R13 = Resistor [tolerance=±5% resistance=1M package=THT]
  R14 = Resistor [tolerance=±5% resistance=100k package=THT]
  R15 = Resistor [tolerance=±5% resistance=100k package=THT]
  R16 = Resistor [tolerance=±5% resistance=1M package=THT]
  U7 = POT [package=pot_alpha_rv16af-20]

nets:
  GND: MCU.GND, MCU.GND1, U4.1IN+, U4.VCC-, U4.4IN+, U6.A, U8.A, U9.A, C2.-, C3.+, C4.+, C5.-, J1.pin1, J2.pin1, C8.0, C9.0, C10.-, C11.-, J3.pin1, J4.pin1, J5.pin1, J6.pin1, R8.Pin_1, C12.-, U7.A
  Diode_Sig_0: MCU.A7/D21, U4.3OUT, R16.Pin_1
  Diode_Sig_1: MCU.A8/D22, U4.2OUT, R10.Pin_1
  N1: MCU.3V3, MCU.3V3_1
  5V/VIN: MCU.Vin, U4.VCC+, C12.+, R11.Pin_0, R14.Pin_0
  DAC_0: MCU.A21/DAC0, R6.Pin_0
  DAC_1: MCU.A22/DAC1, R3.Pin_0
  N2: U4.1OUT, R9.Pin_0, U7.E
  N3: U4.1IN-, J5.pin2, R9.Pin_1
  N4: U4.2IN+, U7.S
  N5: U4.2IN-, R10.Pin_0, R12.Pin_1
  N6: U4.3IN-, R15.Pin_1, R16.Pin_0
  N7: U4.3IN+, U9.S
  N8: U4.4IN-, J6.pin2, R13.Pin_1
  N9: U4.4OUT, U9.E, R13.Pin_0
  N10: U6.S, R12.Pin_0
  N11: U6.E, R11.Pin_1
  N12: U8.S, R15.Pin_0
  N13: U8.E, R14.Pin_1
  -12V: U1.V-, U10.connector3, R1.Pin_1, C3.-, U11.V-, R2.Pin_1, C4.-, C11.+, J3.pin2
  12V: U1.V+, U10.connector7, C2.+, U11.V+, C5.+, C10.+, J4.pin2, R7.Pin_1
  N14: U1.Vo, U1.IN-, J1.pin2, C8.1
  N15: U1.IN+, U10.connector0, R4.Pin_1
  N16: U1.I-LIM, R1.Pin_0
  N17: U10.connector1, R3.Pin_1, R4.Pin_0
  N18: U10.connector2, U10.connector4, R7.Pin_0, R8.Pin_0
  N19: U10.connector5, R5.Pin_0, R6.Pin_1
  N20: U10.connector6, U11.IN+, R5.Pin_1
  N21: U11.Vo, U11.IN-, J2.pin2, C9.1
  N22: U11.I-LIM, R2.Pin_0

notes:
  Coil 0
  Coil 1
  +12
  -12V
  DAC 1
  DAC 0
  Vin (5v)
  Diode 0
  Diode 1
  Gain 0
  Offset 0
  Gain 1
  Offset 1
  Gain
  Offset
  Wall Converters
  AWESEM, Photodiode Transresistive Amplifiers, 0.0
  AWESEM, Coil Driver Amplifiers, 0.0
  AWESEM, Top Sheet, 0.0
  NOTES:
  - Currently only SIG_1 is used.
  - VIN is from USB (5.0 V) unless a jumper is cut and otherwise can be supplied with an external power source from 4.0V to 6.3V. VIN is converted to the required 3.3V logic voltage for the rest of the Teensy 3.6.
  - All IO pins on the Teensy 3.6 are 3.3V tolerant only, do not apply more than 3.3V to any logic or analog pin.
  Diode Orientation
  10kΩ

custom parts:
  Teensy 3.6 (Basic): The Teensy is a complete USB-based microcontoller development system, in a very small footprint, capable of implementing many types of projects. All programming is done via the USB port. No special programmer is needed, only a standard micro-USB cable and a PC or Macintosh with a USB port.
  OPA548: OPA548. High-voltage, high-current operational amplifier
