# Fritzing sketch PhotodiodeAmp_BPW21R_SingleChannel (saved by Fritzing 0.9.3b)
breadboards: 1

parts:
  IC1 = IC, DIP package, 14 pins [chip_label=GL324]
  R1 = Resistor [tolerance=±5% resistance=100k package=THT]
  R2 = Rotary Potentiometer (Large) [maximum_resistance=1MΩ package=THT]
  P1 = S1133 Si Photodiode [package="8mm Ceramic [THT]"]
  J1 = Screw terminal - 2 pins [package=THT]
  BATT1 = 3xAAA Switchable Battery Pack w/Bare Wire

nets:
  N1: IC1.pin1, R2.leg1, J1.pin2
  N2: IC1.pin2, R1.Pin_1, R2.wiper
  GND: IC1.pin3, IC1.pin11, P1.anode, J1.pin1, BATT1.NEG
  4.5V: IC1.pin4, BATT1.POS
  N3: R1.Pin_0, P1.cathode

notes:
  Detector
  To MCU

custom parts:
  3xAAA Switchable Battery Pack w/Bare Wire: 3xAAA Switchable Battery Pack w/Bare Wire Connectors
